// Logisim project a.circ as structural Verilog: 1 circuit, main circuit main
module main (
  input  in_1,
  input  in_2,
  input  [5:0] in_3,
  output [9:0] out_4
);

  wire and_1_out, and_2_out, and_3_out, and_4_out, and_5_out, and_6_out, clock_1_out, clock_2_out,
       comparator_1_eq, comparator_1_lt, multiplexer_1_out, nor_1_out, nor_2_out, nor_3_out, nor_4_out,
       nor_5_out, nor_6_out, or_1_out;
  wire [5:0] counter_1_q, multiplexer_2_out, multiplexer_3_out;
  wire [9:0] bit_extender_1_out, register_1_q;

  Clock clock_1 (.out(clock_1_out));
  Multiplexer multiplexer_1 (.in0(clock_1_out), .in1(1'b0), .out(multiplexer_1_out), .sel(nor_1_out));  // open: en
  Counter #(.width(6), .max('h3f)) counter_1 (
    .D(counter_1_q), .Q(counter_1_q), .clk(multiplexer_1_out), .clr(in_2));  // open: load, count, carry
  Comparator #(.width(6), .mode("unsigned")) comparator_1 (
    .a(counter_1_q), .b(in_3), .eq(comparator_1_eq), .lt(comparator_1_lt));  // open: gt
  Multiplexer #(.width(6)) multiplexer_2 (
    .in0(counter_1_q), .in1({6{1'b0}}), .out(multiplexer_2_out), .sel(nor_1_out));  // open: en
  nor nor_1 (nor_1_out, comparator_1_eq, comparator_1_lt);
  nor nor_2 (nor_2_out, ~multiplexer_2_out[1], multiplexer_2_out[2], multiplexer_2_out[3], multiplexer_2_out[4], multiplexer_2_out[5]);  // NOR_Gate
  nor nor_3 (nor_3_out, ~multiplexer_2_out[0], ~multiplexer_2_out[1], multiplexer_2_out[2], multiplexer_2_out[4], multiplexer_2_out[5]);  // NOR_Gate
  nor nor_4 (nor_4_out, ~multiplexer_2_out[0], multiplexer_2_out[1], ~multiplexer_2_out[2], multiplexer_2_out[4], multiplexer_2_out[5]);  // NOR_Gate
  nor nor_5 (nor_5_out, ~multiplexer_2_out[0], multiplexer_2_out[1], ~multiplexer_2_out[2], multiplexer_2_out[3], multiplexer_2_out[4]);  // NOR_Gate
  nor nor_6 (nor_6_out, ~multiplexer_2_out[0], multiplexer_2_out[2], multiplexer_2_out[3], ~multiplexer_2_out[4], multiplexer_2_out[5]);  // NOR_Gate
  and and_1 (and_1_out, multiplexer_2_out[0], ~multiplexer_2_out[2], multiplexer_2_out[3], ~multiplexer_2_out[4], multiplexer_2_out[5]);  // AND_Gate
  and and_2 (and_2_out, multiplexer_2_out[0], multiplexer_2_out[2], multiplexer_2_out[3], multiplexer_2_out[4], ~multiplexer_2_out[5]);  // AND_Gate
  and and_3 (and_3_out, multiplexer_2_out[0], multiplexer_2_out[1], multiplexer_2_out[3], ~multiplexer_2_out[4], multiplexer_2_out[5]);  // AND_Gate
  and and_4 (and_4_out, multiplexer_2_out[0], multiplexer_2_out[1], ~multiplexer_2_out[2], multiplexer_2_out[3], multiplexer_2_out[5]);  // AND_Gate
  and and_5 (and_5_out, multiplexer_2_out[0], ~multiplexer_2_out[1], multiplexer_2_out[2], multiplexer_2_out[4], multiplexer_2_out[5]);  // AND_Gate
  and and_6 (and_6_out, multiplexer_2_out[0], multiplexer_2_out[1], ~multiplexer_2_out[3], ~multiplexer_2_out[5]);  // AND_Gate
  Multiplexer #(.width(6)) multiplexer_3 (
    .in0({6{1'b0}}), .in1(multiplexer_2_out), .out(multiplexer_3_out), .sel(or_1_out));  // open: en
  or or_1 (or_1_out, nor_2_out, nor_3_out, nor_4_out, nor_5_out, nor_6_out, and_1_out, and_2_out, and_3_out, and_4_out, and_5_out, and_6_out);
  Clock clock_2 (.out(clock_2_out));
  assign bit_extender_1_out = {{4{1'b0}}, multiplexer_3_out};  // Bit_Extender bit_extender_1
  Register #(.width(10)) register_1 (.D(out_4), .en(1'b1), .Q(register_1_q), .clk(clock_2_out), .clr(in_1));
  Adder #(.width(10)) adder_1 (.a(bit_extender_1_out), .b(register_1_q), .out(out_4));  // open: cin, cout
endmodule
